# Fritzing sketch Controlling LED by PWM (saved by Fritzing 0.8.7b)
breadboards: 1

parts:
  R1 = Resistor [tolerance=±5% resistance=220 package=THT]
  LED1 = LED - 5mm [color="Red (633nm)" package="5 mm [THT]"]
  元件1 = Arduino Uno (Rev3) - ICSP

nets:
  N1: R1.Pin_0, 元件1.D9_PWM
  N2: R1.Pin_1, LED1.anode
  N3: LED1.cathode, 元件1.GND
