# Fritzing sketch Controlling LED by Potentiometer (saved by Fritzing 0.8.7b)
breadboards: 1

parts:
  R1 = Resistor [tolerance=±5% resistance=220 package=THT]
  LED_RED = LED - 5mm [color="Red (633nm)" package="5 mm [THT]"]
  R2 = Rotary Potentiometer (Small) [maximum_resistance=100kΩ package=THT]
  元件2 = Arduino Uno (Rev3) - ICSP

nets:
  N1: R1.Pin_0, LED_RED.anode
  N2: R1.Pin_1, 元件2.D9_PWM
  N3: LED_RED.cathode, R2.leg2, 元件2.GND
  N4: R2.leg1, 元件2.5V
  N5: R2.wiper, 元件2.A0
