# Fritzing sketch DC Motor Control_simple (saved by Fritzing 0.8.7b)
circuit board: 8.46667cm x 5.64444cm
breadboards: 1

parts:
  IC1 = L293D [package=THT]
  M1 = DC Motor
  元件3 = Arduino Uno (Rev3) - ICSP

nets:
  N1: IC1.Enable_1, IC1.+Vmotor, 元件3.5V
  N2: IC1.In_1, 元件3.D10_PWM/SS
  N3: IC1.Out_1_(_Controlled_by_Enable_1_), M1.pin_2
  N4: IC1.0V, 元件3.GND
  N5: IC1.Out_2_(_Controlled_by_Enable_1_), M1.pin_1
  N6: IC1.In_2, 元件3.D9_PWM
