# Fritzing sketch LCD1602 (saved by Fritzing 0.8.7b)
breadboards: 1

parts:
  R4 = Rotary Potentiometer (Small) [maximum_resistance=100kΩ package=THT]
  元件1 = Arduino Uno (Rev3) - ICSP
  U1 = LCD-16X2 [package=lcd-16x2]

nets:
  5V: R4.leg1, 元件1.5V, U1.VDD
  N1: R4.wiper, U1.VO
  GND: R4.leg2, 元件1.GND, U1.VSS, U1.R_W, U1.K
  N2: 元件1.D10_PWM/SS, U1.DB4
  N3: 元件1.D11_PWM/MOSI, U1.DB5
  N4: 元件1.D12/MISO, U1.DB6
  N5: 元件1.D13/SCK, U1.DB7
  N6: 元件1.D4, U1.RS
  N7: 元件1.D6_PWM, U1.E
  N8: 元件1.3V3, U1.A
