# Fritzing sketch Serial Monitor (saved by Fritzing 0.8.7b)
breadboards: 1

parts:
  LED1 = LED - 5mm [color="Red (633nm)" package="5 mm [THT]"]
  LED2 = LED - 5mm [color="Yellow (595nm)" package="5 mm [THT]"]
  LED3 = LED - 5mm [color="Green (570nm)" package="5 mm [THT]"]
  R1 = Resistor [tolerance=±5% resistance=220 package=THT]
  R2 = Resistor [tolerance=±5% resistance=220 package=THT]
  R3 = Resistor [tolerance=±5% resistance=220 package=THT]
  元件1 = Arduino Uno (Rev3) - ICSP

nets:
  N1: LED1.cathode, LED2.cathode, LED3.cathode, 元件1.GND
  N2: LED1.anode, R1.Pin_1
  N3: LED2.anode, R2.Pin_1
  N4: LED3.anode, R3.Pin_1
  N5: R1.Pin_0, 元件1.D4
  N6: R2.Pin_0, 元件1.D3_PWM
  N7: R3.Pin_0, 元件1.D2
