# Fritzing sketch 7-Segment Display (saved by Fritzing 0.8.7b)
breadboards: 1

parts:
  R1 = Resistor [tolerance=±5% resistance=220 package=THT]
  R2 = Resistor [tolerance=±5% resistance=220 package=THT]
  R3 = Resistor [tolerance=±5% resistance=220 package=THT]
  R4 = Resistor [tolerance=±5% resistance=220 package=THT]
  R5 = Resistor [tolerance=±5% resistance=220 package=THT]
  R6 = Resistor [tolerance=±5% resistance=220 package=THT]
  R7 = Resistor [tolerance=±5% resistance=220 package=THT]
  R8 = Resistor [tolerance=±5% resistance=220 package=THT]
  DI1 = 7-Segment LED Display [package=THT]
  元件1 = Arduino Uno (Rev3) - ICSP

nets:
  N1: R1.Pin_0, DI1.cathodeB
  N2: R1.Pin_1, 元件1.D6_PWM
  N3: R2.Pin_0, DI1.cathodeA
  N4: R2.Pin_1, 元件1.D7
  N5: R3.Pin_0, 元件1.D8
  N6: R3.Pin_1, DI1.cathodeF
  N7: R4.Pin_0, 元件1.D9_PWM
  N8: R4.Pin_1, DI1.cathodeG
  N9: R5.Pin_0, 元件1.D11_PWM/MOSI
  N10: R5.Pin_1, DI1.cathodeD
  N11: R6.Pin_0, 元件1.D10_PWM/SS
  N12: R6.Pin_1, DI1.cathodeE
  N13: R7.Pin_0, DI1.cathodeDP
  N14: R7.Pin_1, 元件1.D4
  N15: R8.Pin_0, DI1.cathodeC
  N16: R8.Pin_1, 元件1.D5_PWM
  N17: DI1.commAnode#2, 元件1.GND
