# Fritzing sketch ne555 (saved by Fritzing 0.8.7b)
breadboards: 1

parts:
  IC1 = General purpose bipolar Timer [package=dil-08]
  C1 = Ceramic Capacitor [capacitance=100nF package="100 mil [THT, multilayer]"]
  R1 = Rotary Potentiometer (Small) [maximum_resistance=100kΩ package=THT]
  R2 = Resistor [tolerance=±5% resistance=10k package=THT]
  C2 = Ceramic Capacitor [capacitance=100nF package="100 mil [THT, multilayer]"]
  元件1 = Arduino Uno (Rev3) - ICSP

nets:
  GND: IC1.GND, C1.0, C2.1, 元件1.GND
  N1: IC1.TRI, IC1.TRE, C1.1, R1.leg1
  N2: IC1.OUT, 元件1.D7
  N3: IC1._RES, IC1.VCC+, R2.Pin_0, 元件1.5V
  N4: IC1.CON, C2.0
  N5: IC1.DIS, R1.wiper, R2.Pin_1

notes:
  NE555
  104
