# Fritzing sketch ADXL335 (saved by Fritzing 0.8.7b)

parts:
  元件3 = Triple Axis Accelerometer Breakout - ADXL335
  元件1 = Arduino Uno (Rev3) - ICSP

nets:
  N1: 元件3.ZOUT, 元件1.A2
  N2: 元件3.YOUT, 元件1.A1
  N3: 元件3.XOUT, 元件1.A0
  GND: 元件3.GND, 元件1.GND
  VCC: 元件3.VCC, 元件1.3V3
