# Fritzing sketch Light Alarm (saved by Fritzing 0.8.7b)
breadboards: 1

parts:
  J1 = Piezo Speaker
  Q1 = NPN-Transistor [package="TO92 [THT]"]
  R1 = Resistor [tolerance=±5% resistance=10k package=THT]
  LED1 = LED - 5mm [color="Red (633nm)" package="5 mm [THT]"]
  元件1 = Arduino Uno (Rev3) - ICSP

nets:
  N1: J1.pin1, R1.Pin_1, LED1.cathode, 元件1.GND
  N2: J1.pin2, 元件1.D5_PWM
  N3: Q1.E, 元件1.5V
  N4: Q1.B, LED1.anode
  N5: Q1.C, R1.Pin_0, 元件1.A0
