# Fritzing sketch Simple Creation - Traffic Light (saved by Fritzing 0.8.7b)
breadboards: 1

parts:
  元件1 = Arduino Uno (Rev3)
  RE1 = Rotary Encoder [package=THT]
  R1 = Resistor [tolerance=±5% resistance=220 package=THT]
  C1 = Ceramic Capacitor [capacitance=100nF package="100 mil [THT, multilayer]"]
  R3 = Resistor [tolerance=±5% resistance=220 package=THT]
  C2 = Ceramic Capacitor [capacitance=100nF package="100 mil [THT, multilayer]"]
  R4 = Resistor [tolerance=±5% resistance=220 package=THT]
  R5 = Resistor [tolerance=±5% resistance=220 package=THT]
  R6 = Resistor [tolerance=±5% resistance=220 package=THT]
  yellow = LED - 5mm [color="Yellow (595nm)" package="5 mm [THT]"]
  red = LED - 5mm [color="Red (633nm)" package="5 mm [THT]"]
  green = LED - 5mm [color="Green (570nm)" package="5 mm [THT]"]

nets:
  N1: 元件1.D8, R5.Pin_0
  N2: 元件1.D9_PWM, R4.Pin_0
  N3: 元件1.GND, RE1.EncoderPinC, C1.1, C2.0, yellow.cathode, red.cathode, green.cathode
  N4: 元件1.D2, RE1.EncoderPinB, R1.Pin_0, C1.0
  N5: 元件1.D3_PWM, RE1.EncoderPinA, R3.Pin_1, C2.1
  N6: 元件1.D7, R6.Pin_0
  N7: 元件1.5V, R1.Pin_1, R3.Pin_0
  N8: R4.Pin_1, green.anode
  N9: R5.Pin_1, yellow.anode
  N10: R6.Pin_1, red.anode
