# Fritzing sketch Simple Creation - Digital Dice (saved by Fritzing 0.8.7b)
breadboards: 1

parts:
  R1 = Resistor [tolerance=±5% resistance=220 package=THT]
  R2 = Resistor [tolerance=±5% resistance=220 package=THT]
  R3 = Resistor [tolerance=±5% resistance=220 package=THT]
  R4 = Resistor [tolerance=±5% resistance=220 package=THT]
  R5 = Resistor [tolerance=±5% resistance=220 package=THT]
  R6 = Resistor [tolerance=±5% resistance=220 package=THT]
  R7 = Resistor [tolerance=±5% resistance=220 package=THT]
  U1 = 74HC595 [package="DIP16 [THT]"]
  DI1 = 7-Segment LED Display [package=THT]
  R8 = Resistor [tolerance=±5% resistance=220 package=THT]
  S1 = Pushbutton [package="[THT]"]
  R9 = Resistor [tolerance=±5% resistance=10k package=THT]
  C1 = Ceramic Capacitor [capacitance=100nF package="100 mil [THT, multilayer]"]
  元件1 = Arduino Uno (Rev3) - ICSP

nets:
  N1: R1.Pin_0, U1.Q1
  N2: R1.Pin_1, DI1.cathodeG
  N3: R2.Pin_0, U1.Q4
  N4: R2.Pin_1, DI1.cathodeD
  N5: R3.Pin_0, DI1.cathodeC
  N6: R3.Pin_1, U1.Q5
  N7: R4.Pin_0, U1.Q2
  N8: R4.Pin_1, DI1.cathodeF
  N9: R5.Pin_0, DI1.cathodeDP
  N10: R5.Pin_1, U1.Q0
  N11: R6.Pin_0, DI1.cathodeA
  N12: R6.Pin_1, U1.Q7
  N13: R7.Pin_0, U1.Q3
  N14: R7.Pin_1, DI1.cathodeE
  N15: U1.Q6, R8.Pin_1
  GND: U1.GND, U1.OE, DI1.commAnode#2, R9.Pin_1, C1.1, 元件1.GND
  VCC: U1.Q7', U1.VCC, S1.Pin_3, S1.Pin_4, 元件1.5V
  N16: U1.SH_CP, 元件1.D8
  N17: U1.ST_CP, 元件1.D12/MISO
  N18: U1.DS, 元件1.D11_PWM/MOSI
  N19: DI1.cathodeB, R8.Pin_0
  N20: S1.Pin_1, S1.Pin_2, R9.Pin_0, C1.0, 元件1.D2
