# Fritzing sketch Small Fan_simple (saved by Fritzing 0.8.7b)
circuit board: 8.46667cm x 5.64444cm
breadboards: 1

parts:
  IC1 = L293D [package=THT]
  M1 = DC Motor
  S2 = Pushbutton [package="[THT]"]
  C2 = Ceramic Capacitor [capacitance=100nF package="100 mil [THT, multilayer]"]
  R6 = Resistor [tolerance=±5% resistance=10k package=THT]
  元件2 = Arduino Uno (Rev3) - ICSP

nets:
  N1: IC1.Enable_1, IC1.+Vmotor, S2.Pin_3, S2.Pin_4, 元件2.5V
  N2: IC1.In_1, 元件2.D10_PWM/SS
  N3: IC1.Out_1_(_Controlled_by_Enable_1_), M1.pin_2
  N4: IC1.0V, C2.1, R6.Pin_1, 元件2.GND
  N5: IC1.Out_2_(_Controlled_by_Enable_1_), M1.pin_1
  N6: IC1.In_2, 元件2.D9_PWM
  N7: S2.Pin_1, S2.Pin_2, C2.0, R6.Pin_0, 元件2.D2
